# Fritzing sketch MIDIIItapeIIMIDI (saved by Fritzing 0.9.3b)
circuit board: 5.66161cm x 5.66743cm
breadboards: 1

parts:
  LM358 = LM 358 Dual Op-Amp [package="DIP8 [THT]"]
  MIDI_In = DIN-5 jack (MIDI) [package=THT]
  MIDI_Out = DIN-5 jack (MIDI) [package=THT]
  R1 = Resistor [tolerance=±5% resistance=10k package=THT]
  R2 = Resistor [tolerance=±5% resistance=1k package=THT]
  R3 = Resistor [tolerance=±5% resistance=4.7k package=THT]
  R4 = Resistor [tolerance=±5% resistance=750 package=THT]
  6N137 = 6n137 Optocoupler [package="DIP (Dual Inline) [THT]"]
  R7 = Resistor [tolerance=±5% resistance=220 package=THT]
  R8 = Resistor [tolerance=±5% resistance=220 package=THT]
  R9 = Resistor [tolerance=±5% resistance=1k package=THT]
  R12 = Resistor [tolerance=±5% resistance=560 package=THT]
  5_1v_Z1 = DIODE-ZENER [part_number=5.1v package=diode-zener]
  D1 = Rectifier Diode [part_number=1N4001 package="300 mil [THT]"]
  R13 = Resistor [tolerance=±5% resistance=220 package=THT]
  R14 = Resistor [tolerance=±5% resistance=1.2k package=THT]
  R15 = Resistor [tolerance=±5% resistance=2.7k package=THT]
  C1 = Tantalum Capacitor [capacitance=47pF package="100 mil [THT, tantalum]"]
  1k_Pot = Rotary Potentiometer (Small) [maximum_resistance=1kΩ package=THT]
  From_Tape = RCA [package=rca]
  To_Tape = RCA [package=rca]
  +5_G_+9 = Header 3 [package=screwterminal-3.5mm-3_lock.007s]

nets:
  N1: LM358.connector0, R4.Pin_0, R12.Pin_0
  N2: LM358.connector1, R2.Pin_0, R3.Pin_1
  N3: LM358.connector2, R1.Pin_0, From_Tape.SHELL
  GND: LM358.connector3, MIDI_In.GND, MIDI_Out.GND, R1.Pin_1, R2.Pin_1, 6N137.GND, R9.Pin_1, 5_1v_Z1.A, C1.-, 1k_Pot.leg1, From_Tape.PIN, To_Tape.PIN, +5_G_+9.2
  N4: LM358.connector4, 6N137.Vo, R7.Pin_1, C1.+
  N5: LM358.connector5, R9.Pin_0, R14.Pin_0
  N6: LM358.connector6, R14.Pin_1, R15.Pin_0
  N7: LM358.connector7, +5_G_+9.3
  N8: MIDI_In.5, 6N137.Vf-, D1.anode
  N9: MIDI_In.4, R8.Pin_0
  N10: MIDI_Out.5, R12.Pin_1, 5_1v_Z1.C
  N11: MIDI_Out.4, R13.Pin_1
  N12: R3.Pin_0, R4.Pin_1
  N13: 6N137.Vf+, R8.Pin_1, D1.cathode
  N14: R7.Pin_0, R13.Pin_0, +5_G_+9.1
  N15: R15.Pin_1, 1k_Pot.leg2
  N16: 1k_Pot.wiper, To_Tape.SHELL

notes:
  MIDI
  II
  TAPE
  ©2025
  Crunchysteve
  No rights reserved
  A Free, Open Source Deign
  gnd
  out
  In
  nc

custom parts:
  6n137 Optocoupler: 6n137 fast Optocoupler. With 8 pins on a 300mil dual inline package (DIP) footprint. Ve is strobe input. Output is inverting.
